# Fritzing sketch Button_wiring (saved by Fritzing 0.9.2b)
breadboards: 1

parts:
  Part1 = Arduino Uno (Rev3) - ICSP
  RED = Momentary Switch [package=ksa_sealed_tac_switch]
  YELLOW = Momentary Switch [package=ksa_sealed_tac_switch]
  YELLOW1 = Momentary Switch [package=ksa_sealed_tac_switch]
  YELLOW2 = Momentary Switch [package=ksa_sealed_tac_switch]

nets:
  N1: Part1.D2, YELLOW2.1
  N2: Part1.D3_PWM, YELLOW1.1
  N3: Part1.D4, YELLOW.1
  N4: Part1.D5_PWM, RED.1
  N5: Part1.GND, RED.3, YELLOW.3, YELLOW1.3, YELLOW2.3

notes:
  RED
  YELLOW
  GREEN
  BLUE
