# Fritzing sketch Button_wiring_with_pullup (saved by Fritzing 0.9.2b)
breadboards: 1

parts:
  Part1 = Arduino Uno (Rev3) - ICSP
  RED = Momentary Switch [package=ksa_sealed_tac_switch]
  R1 = Resistor [tolerance=±5% resistance=22k package=THT]
  YELLOW = Momentary Switch [package=ksa_sealed_tac_switch]
  R2 = Resistor [tolerance=±5% resistance=22k package=THT]
  YELLOW1 = Momentary Switch [package=ksa_sealed_tac_switch]
  R3 = Resistor [tolerance=±5% resistance=22k package=THT]
  YELLOW2 = Momentary Switch [package=ksa_sealed_tac_switch]
  R4 = Resistor [tolerance=±5% resistance=22k package=THT]

nets:
  N1: Part1.D2, YELLOW2.1, R4.Pin_1
  N2: Part1.D3_PWM, YELLOW1.1, R3.Pin_1
  N3: Part1.D4, YELLOW.1, R2.Pin_1
  N4: Part1.D5_PWM, RED.1, R1.Pin_1
  N5: Part1.5V, R1.Pin_0, R2.Pin_0, R3.Pin_0, R4.Pin_0
  N6: Part1.GND, RED.3, YELLOW.3, YELLOW1.3, YELLOW2.3

notes:
  RED
  YELLOW
  GREEN
  BLUE
